// Logisim project pulseDifferentialCircuit.circ as structural Verilog: 1 circuit, main circuit main
module main (
  input  ADD,
  input  SUB,
  output out_3
);

  wire and_2_out, and_3_out, clock_1_out, d_ff_1_qn, d_ff_2_qn, not_1_out, or_1_out, Q0_qn;

  Clock clock_1 (.out(clock_1_out));
  D_Flip_Flop Q0 (.clk(clock_1_out), .D(ADD), .Qn(Q0_qn));  // open: Q, preset, en, reset
  D_Flip_Flop d_ff_1 (.clk(clock_1_out), .D(ADD), .Qn(d_ff_1_qn));  // open: Q, preset, en, reset
  D_Flip_Flop d_ff_2 (.clk(clock_1_out), .D(SUB), .Qn(d_ff_2_qn));  // open: Q, preset, en, reset
  and and_1 (out_3, ADD, Q0_qn);
  and and_2 (and_2_out, ADD, d_ff_1_qn);
  and and_3 (and_3_out, d_ff_2_qn, SUB);
  not not_1 (not_1_out, out_3);
  or or_1 (or_1_out, and_2_out, and_3_out);
  Counter counter_1 (.load(not_1_out), .count(1'b1), .clk(or_1_out));  // open: D, Q, carry, clr
endmodule
